# Fritzing sketch circuit-breadboard (saved by Fritzing 0.9.3b)
circuit board: 8.46667cm x 5.64444cm
breadboards: 1

parts:
  Bauteil1 = Arduino Mega 2560 (Rev3)
  J1 = female pin header, 2 pins [form="♀ (female)"]
  R1 = Resistor [tolerance=±5% resistance=10k package=THT]
  C1 = Electrolytic Capacitor [capacitance=22µF package="100 mil [THT, electrolytic]"]
  R2 = Resistor [tolerance=±5% resistance=10k package=THT]
  R3 = Resistor [tolerance=±5% resistance=10k package=THT]
  VCC1 = Battery block 9V
  C2 = Electrolytic Capacitor [capacitance=22µF package="100 mil [THT, electrolytic]"]
  R5 = Resistor [tolerance=±5% resistance=10k package=THT]
  R6 = Resistor [tolerance=±5% resistance=10k package=THT]
  R4 = Resistor [tolerance=±5% resistance=10k package=THT]
  U1 = LM 358 Dual Op-Amp [package="DIP8 [THT]"]
  R7 = Resistor [tolerance=±5% resistance=10k package=THT]
  S1 = Pushbutton [package="[THT]"]

nets:
  GND: Bauteil1.GND, C1.-, R2.Pin_0, VCC1.-, C2.-, R5.Pin_0, U1.connector3, R7.Pin_1
  N1: Bauteil1.D2_PWM, R4.Pin_0
  N2: Bauteil1.D3_PWM, R1.Pin_0
  5V Arduino: Bauteil1.5V, S1.Pin_1, S1.Pin_2
  N3: Bauteil1.D22, R7.Pin_0, S1.Pin_3, S1.Pin_4
  N4: J1.pin1, R3.Pin_1, U1.connector0
  N5: J1.pin2, R6.Pin_1, U1.connector6
  N6: R1.Pin_1, C1.+, U1.connector2
  N7: R2.Pin_1, R3.Pin_0, U1.connector1
  N8: VCC1.+, U1.connector7
  N9: C2.+, R4.Pin_1, U1.connector4
  N10: R5.Pin_1, R6.Pin_0, U1.connector5

notes:
  Option - Food Break Switch

// code stored in the sketch: complex-v1.ino
/*
  Fade

  This example shows how to fade an LED on pin 9 using the analogWrite()
  function.

  The analogWrite() function uses PWM, so if you want to change the pin you're
  using, be sure to use another PWM capable pin. On most Arduino, the PWM pins
  are identified with a "~" sign, like ~3, ~5, ~6, ~9, ~10 and ~11.

  This example code is in the public domain.

  http://www.arduino.cc/en/Tutorial/Fade
*/

int pump1 = 3;           // the PWM pin the controller is attached to
int pump1Min = 10;
int pump1Max = 200;
int pump1Current = 0;
int brightness = 10;    // how bright the LED is
int fadeAmount = 5;    // how many points to fade the LED by
int t1 = 1; // time in secs. to stay at level min
int t2 = 2; // time in secs. to stay at max
int t3 = 1; // time in secs. to go from min to max
int t4 = 1; // time in secs. to go from max to min
char step = 't1'; // step marker

// the setup routine runs once when you press reset:
void setup() {
  // declare pin 9 to be an output:
  pinMode(pump1, pump1Current);
}



// the loop routine runs over and over again forever:
void loop() {
  pump1();
  //pumpOn();
  //delay(300);
  //pumpOff();
  //delay(500);
}

void pump1() {
  
}
void pumpOn() {
  // set the brightness of pin 9:
  analogWrite(pump1, brightness);

  // change the brightness for next time through the loop:
  brightness = brightness + fadeAmount;

  // reverse the direction of the fading at the ends of the fade:
  if (brightness <= 0 || brightness >= 255) {
    fadeAmount = -fadeAmount;
  }
  // wait for 30 milliseconds to see the dimming effect
  delay(10);
}
void pumpOff() {
  // set the brightness of pin 9:
  analogWrite(pump1, brightness);

  // change the brightness for next time through the loop:
  brightness = brightness - fadeAmount;

  // reverse the direction of the fading at the ends of the fade:
  if (brightness <= 0 || brightness >= 255) {
    fadeAmount = -fadeAmount;
  }
  // wait for 30 milliseconds to see the dimming effect
  delay(30);
}
